# Fritzing sketch trasmettitore go kart circuito (saved by Fritzing 0.9.3b)

parts:
  Componente1 = Arduino Uno (Rev3)
  S1 = Momentary Switch [package=ksa_sealed_tac_switch]
  S2 = Momentary Switch [package=ksa_sealed_tac_switch]
  S3 = Momentary Switch [package=ksa_sealed_tac_switch]
  S4 = Momentary Switch [package=ksa_sealed_tac_switch]
  S5 = Momentary Switch [package=ksa_sealed_tac_switch]
  S6 = Momentary Switch [package=ksa_sealed_tac_switch]
  BAT1 = 18650 battery holder [package=battery-18650-kit]
  BAT2 = 18650 battery holder [package=battery-18650-kit]
  U1 = SWITCH_SPDT [package=kps-1290]
  Componente2 = NRF24L01+ Breakout Board

nets:
  N1: Componente1.A0, S1.4
  N2: Componente1.A1, S2.4
  N3: Componente1.A2, S3.4
  N4: Componente1.A3, S4.4
  N5: Componente1.A4/SDA, S5.4
  N6: Componente1.A5/SCL, S6.4
  N7: Componente1.D9_PWM, Componente2.CE
  N8: Componente1.D10_PWM/SS, Componente2.CS
  N9: Componente1.D11_PWM/MOSI, Componente2.MOSI
  N10: Componente1.D12/MISO, Componente2.MISO
  N11: Componente1.D13/SCK, Componente2.SCK
  GND: Componente1.GND, S1.1, S2.1, S3.1, S4.1, S5.1, S6.1, BAT2.-, Componente2.GND
  3V3: Componente1.3V3, Componente2.VCC
  N12: Componente1.VIN, U1.S
  N13: BAT1.+, U1.P
  N14: BAT1.-, BAT2.+

custom parts:
  18650 battery holder: 18650 Battery Holder
